# Fritzing sketch LED Sketch (saved by Fritzing 0.4.2b)
breadboards: 1

parts:
  Arduino1 = Arduino
  LED1 = Red LED - 5mm
  R1 = Resistor [resistance=220 package=THT]

nets:
  N1: Arduino1.GND, LED1.cathode
  N2: Arduino1.+5V, R1.Pin_0
  N3: LED1.anode, R1.Pin_1
