# Fritzing sketch LED Sketch (saved by Fritzing 0.4.2b)
breadboards: 1

parts:
  Arduino1 = Arduino
  R1 = Resistor [resistance=220 package=THT]
  LED1 = Red LED - 5mm

nets:
  N1: Arduino1.GND, LED1.cathode
  N2: Arduino1.D11, R1.Pin_0
  N3: R1.Pin_1, LED1.anode
