# Fritzing sketch RGB LED Sketch (saved by Fritzing 0.4.2b)
breadboards: 1

parts:
  Arduino1 = Arduino
  R1_R = Resistor [resistance=220 package=THT]
  R2_G = Resistor [resistance=220 package=THT]
  R3_B = Resistor [resistance=220 package=THT]
  LED1 = RGB LED - (4 legs) [package="5 mm [THT]"]

nets:
  N1: Arduino1.D11, R1_R.Pin_0
  N2: Arduino1.D10, R2_G.Pin_0
  N3: Arduino1.D9, R3_B.Pin_0
  N4: Arduino1.+5V, LED1.common_anode
  N5: R1_R.Pin_1, LED1.red_cathode
  N6: R2_G.Pin_1, LED1.green_cathode
  N7: R3_B.Pin_1, LED1.blue_cathode
